# Fritzing sketch ESP01-breadboard (saved by Fritzing 0.9.3b)
breadboards: 1

parts:
  U1 = ESP8266 WiFi Module [part_number=ESP8266]
  Componente1 = USB converter CP2102
  S1 = Pushbutton [package="[SMD]"]

nets:
  N1: U1.RXD, Componente1.TXO
  VCC: U1.VCC, U1.CH_PD, Componente1.3V3
  GND: U1.GPIO_0, U1.GND, Componente1.GND, S1.Pin_3, S1.Pin_4
  N2: U1.RST, S1.Pin_1, S1.Pin_2
  N3: U1.TXD, Componente1.RXI

notes:
  To enable serial programming GPIO0 should be pulled low

custom parts:
  ESP8266 WiFi Module: Generic WiFi Module based on the ESP8266 with onboard PCB antenna and UART communications
